// Logisim project Part1.circ as structural Verilog: 6 circuits, main circuit main
module main (
  input  in_1,
  input  in_2,
  output out_3
);

  NotAnd notand_1 (.in_1(in_1), .in_2(in_2), .out_3(out_3));
endmodule

module NotAnd (
  input  in_1,
  input  in_2,
  output out_3
);

  wire and_1_out;

  and and_1 (and_1_out, in_1, in_2);
  not not_1 (out_3, and_1_out);
endmodule

module NotOr (
  input  in_1,
  input  in_2,
  output out_3
);

  wire or_1_out;

  or or_1 (or_1_out, in_1, in_2);
  not not_1 (out_3, or_1_out);
endmodule

module X_OR (
  input  in_1,
  input  in_2,
  output out_3
);

  wire and_1_out, and_2_out, not_1_out, not_2_out;

  not not_1 (not_1_out, in_1);
  not not_2 (not_2_out, in_2);
  and and_1 (and_1_out, not_1_out, in_2);
  and and_2 (and_2_out, not_2_out, in_1);
  or or_1 (out_3, and_1_out, and_2_out);
endmodule

module MUX2_1 (
  input  A,
  input  S,
  input  B,
  output out_4
);

  wire and_1_out, and_2_out, not_1_out;

  not not_1 (not_1_out, S);
  and and_1 (and_1_out, not_1_out, A);
  and and_2 (and_2_out, S, B);
  or or_1 (out_4, and_1_out, and_2_out);
endmodule

module MUX4_1 (
  input  A,
  input  C,
  input  S1,
  input  B,
  input  D,
  input  S2,
  output out_7
);

  wire mux2_1_1_out_4, mux2_1_2_out_4;

  MUX2_1 mux2_1_1 (.A(A), .S(S1), .B(C), .out_4(mux2_1_1_out_4));
  MUX2_1 mux2_1_2 (.A(B), .S(S1), .B(D), .out_4(mux2_1_2_out_4));
  MUX2_1 mux2_1_3 (.A(mux2_1_1_out_4), .S(S2), .B(mux2_1_2_out_4), .out_4(out_7));
endmodule
