// Logisim project ALU_starter.circ as structural Verilog: 4 circuits, main circuit main
module main (
  input  [31:0] IN1,
  input  [31:0] IN2,
  input  [2:0] Sel,
  output [31:0] OUT1
);

  ALU alu_1 (.Input1(IN1), .Input2(IN2), .Sel(Sel), .Output1(OUT1));
endmodule

module main_2 (
  input  [31:0] in_1,
  input  [31:0] in_2,
  input  [2:0] in_3,
  output [31:0] out_4
);

  ALU_2 alu_2_1 (.out_4(out_4), .in_3(in_3), .in_2(in_2), .in_1(in_1));
endmodule

module ALU (
  input  [31:0] Input1,
  input  [31:0] Input2,
  input  [2:0] Sel,
  output [31:0] Output1
);

  wire [31:0] and_1_out, or_1_out, shifter_1_out, shifter_2_out, shifter_3_out, shifter_4_out, shifter_5_out,
       xor_1_out;

  Shifter #(.width(32)) shifter_1 (.in(Input1), .\dist (Input2[4:0]), .out(shifter_1_out));
  Shifter #(.width(32), .shift("lr")) shifter_2 (.in(Input1), .\dist (Input2[4:0]), .out(shifter_2_out));
  Shifter #(.width(32), .shift("ar")) shifter_3 (.in(Input1), .\dist (Input2[4:0]), .out(shifter_3_out));
  Shifter #(.width(32), .shift("rl")) shifter_4 (.in(Input1), .\dist (Input2[4:0]), .out(shifter_4_out));
  Shifter #(.width(32), .shift("rr")) shifter_5 (.in(Input1), .\dist (Input2[4:0]), .out(shifter_5_out));
  assign and_1_out = Input1 & Input2;  // AND_Gate and_1, 32 bits wide
  assign or_1_out = Input1 | Input2;  // OR_Gate or_1, 32 bits wide
  assign xor_1_out = Input1 ^ Input2;  // XOR_Gate xor_1, 32 bits wide
  Multiplexer #(.select(3), .width(32), .enable("false")) multiplexer_1 (
    .in0(shifter_1_out), .in1(shifter_2_out), .in2(shifter_3_out), .in3(shifter_4_out), .in4(shifter_5_out),
    .in5(and_1_out), .in6(or_1_out), .in7(xor_1_out), .out(Output1), .sel(Sel));

  // Notes on the sheet:
  //   sll
  //   srl
  //   sra
  //   rl
  //   rr
  //   and
  //   or
  //   xor
endmodule

module ALU_2 (
  input  [31:0] in_1,
  input  [31:0] in_2,
  input  [2:0] in_3,
  output [31:0] out_4
);

  wire [31:0] bit_and, bit_or, bit_xor, rl, rr, shll, shra, shrl;

  assign bit_and = in_1 & in_2;  // AND_Gate and_1, 32 bits wide
  assign bit_or = in_1 | in_2;  // OR_Gate or_1, 32 bits wide
  assign bit_xor = in_1 ^ in_2;  // XOR_Gate xor_1, 32 bits wide
  Shifter #(.width(32)) shifter_1 (.in(in_1), .\dist (in_2[4:0]), .out(shll));
  Shifter #(.width(32), .shift("lr")) shifter_2 (.in(in_1), .\dist (in_2[4:0]), .out(shrl));
  Shifter #(.width(32), .shift("ar")) shifter_3 (.in(in_1), .\dist (in_2[4:0]), .out(shra));
  Shifter #(.width(32), .shift("rl")) shifter_4 (.in(in_1), .\dist (in_2[4:0]), .out(rl));
  Shifter #(.width(32), .shift("rr")) shifter_5 (.in(in_1), .\dist (in_2[4:0]), .out(rr));
  Multiplexer #(.select(3), .width(32), .enable("false")) multiplexer_1 (
    .in0(shll), .in1(shrl), .in2(shra), .in3(rl), .in4(rr), .in5(bit_and), .in6(bit_or), .in7(bit_xor),
    .out(out_4), .sel(in_3));

  // Other names for the same wires on the sheet: in1[31:0] = in_1; in2[31:0] = in_2; in2_5[4:0] = in_2[4:0]

  // Notes on the sheet:
  //   sll
  //   srl
  //   sra
  //   rl
  //   rr
  //   and
  //   or
  //   xor
endmodule
