// Logisim project RotateRight.circ as structural Verilog: 5 circuits, main circuit main
module main (
  input  [15:0] in_1,
  input  [3:0] in_2,
  output [15:0] out_3
);

  wire [15:0] multiplexer_1_out, multiplexer_2_out, multiplexer_3_out, rr_1_1_out_2, rr_2_1_out_2,
       rr_4_1_out_2, rr_8_1_out_2;

  Multiplexer #(.width(16), .enable("false")) multiplexer_1 (
    .in0(in_1), .in1(rr_1_1_out_2), .out(multiplexer_1_out), .sel(in_2[0]));
  RR_1 rr_1_1 (.in_1(in_1), .out_2(rr_1_1_out_2));
  Multiplexer #(.width(16), .enable("false")) multiplexer_2 (
    .in0(multiplexer_1_out), .in1(rr_2_1_out_2), .out(multiplexer_2_out), .sel(in_2[1]));
  RR_2 rr_2_1 (.in_1(multiplexer_1_out), .out_2(rr_2_1_out_2));
  RR_4 rr_4_1 (.in_1(multiplexer_2_out), .out_2(rr_4_1_out_2));
  Multiplexer #(.width(16), .enable("false")) multiplexer_3 (
    .in0(multiplexer_2_out), .in1(rr_4_1_out_2), .out(multiplexer_3_out), .sel(in_2[2]));
  Multiplexer #(.width(16), .enable("false")) multiplexer_4 (
    .in0(multiplexer_3_out), .in1(rr_8_1_out_2), .out(out_3), .sel(in_2[3]));
  RR_8 rr_8_1 (.in_1(multiplexer_3_out), .out_2(rr_8_1_out_2));
endmodule

module RR_1 (
  input  [15:0] in_1,
  output [15:0] out_2
);


  assign out_2 = {in_1[0], in_1[15:1]};
endmodule

module RR_2 (
  input  [15:0] in_1,
  output [15:0] out_2
);


  assign out_2 = {in_1[1:0], in_1[15:2]};
endmodule

module RR_4 (
  input  [15:0] in_1,
  output [15:0] out_2
);


  assign out_2 = {in_1[3:0], in_1[15:4]};
endmodule

module RR_8 (
  input  [15:0] in_1,
  output [15:0] out_2
);


  assign out_2 = {in_1[7:0], in_1[15:8]};
endmodule
