// Logisim project Splitter.circ as structural Verilog: 2 circuits, main circuit Try
module Try (
  output [1:0] out_1,
  output [3:0] out_2,
  output [5:0] out_3,
  output [1:0] out_4,
  output [1:0] out_5
);


  assign out_1 = 2'b01;
  assign out_2 = 4'b1001;
  assign out_3 = 6'b111001;
  assign out_4 = 2'b11;
  assign out_5 = 2'b10;
endmodule

module Ex1 (
  input  [7:0] In1,
  output Out1,
  output [7:0] Out2
);

  and and_1 (Out1, In1[0], In1[7]);
  not not_1 (Out2[7], In1[7]);

  assign Out2[6:0] = In1[6:0];
endmodule
