// Logisim project Fibonacci.circ as structural Verilog: 2 circuits, main circuit main
module main (
  input  [3:0] in_1
);

  wire undriven;

  // Probe on in_1
  Fabonacci fabonacci_1 (.N(in_1));  // open: Fn, out_3, out_4
  // Probe on undriven
endmodule

module Fabonacci (
  input  [3:0] N,
  output [7:0] Fn,
  output [8:0] out_3,
  output [8:0] out_4
);

  wire clock_1_out, clock_2_out, clock_3_out, comparator_1_eq, comparator_2_eq, comparator_3_eq, Enable;
  wire [3:0] adder_1_out, Counter;
  wire [7:0] multiplexer_1_out, multiplexer_2_out, register_2_q, register_3_q;

  Comparator #(.width(4)) comparator_1 (.a(Counter), .b(4'b0000), .eq(comparator_1_eq));  // open: gt, lt
  Comparator #(.width(4)) comparator_2 (.a(Counter), .b(4'b0000), .eq(comparator_2_eq));  // open: gt, lt
  Register #(.width(4)) register_1 (.D(adder_1_out), .en(Enable), .clk(clock_1_out), .Q(Counter));  // open: clr
  Clock clock_1 (.out(clock_1_out));
  Multiplexer #(.width(8), .enable("false")) multiplexer_1 (
    .in0(register_3_q), .in1(8'h1), .out(multiplexer_1_out), .sel(comparator_1_eq));
  Multiplexer #(.width(8), .enable("false")) multiplexer_2 (
    .in0(Fn), .in1({8{1'b0}}), .out(multiplexer_2_out), .sel(comparator_2_eq));
  // Probe on Counter
  Register register_2 (.D(multiplexer_1_out), .en(Enable), .clk(clock_2_out), .Q(register_2_q));  // open: clr
  Clock clock_2 (.out(clock_2_out));
  Register register_3 (.D(multiplexer_2_out), .en(Enable), .clk(clock_3_out), .Q(register_3_q));  // open: clr
  Clock clock_3 (.out(clock_3_out));
  Adder #(.width(4)) adder_1 (.a(Counter), .b(4'b0001), .out(adder_1_out));  // open: cin, cout
  // Probe on register_2_q
  Adder adder_2 (.a(register_2_q), .b(register_3_q), .out(Fn));  // open: cin, cout
  // Probe on register_3_q
  Comparator #(.width(4)) comparator_3 (.a(Counter), .b(N), .eq(comparator_3_eq));  // open: gt, lt
  not not_1 (Enable, comparator_3_eq);
  // Probe on Fn
  // Probe on Enable

  // Notes on the sheet:
  //   Here, we assume F(-1) = 1, for convenience to calculate F1
  //   Fn-2
  //   Fn-1
endmodule
