// Logisim project alu.circ as structural Verilog: 1 circuit, main circuit alu
module alu (
  input  [31:0] A,
  input  [31:0] B,
  input  [3:0] ALUSel,
  output [31:0] Result
);

  wire [0:0] out_slt;
  wire [6:0] out_cnto;
  wire [31:0] adder_2_out, bit_extender_1_out, bit_extender_2_out, multiplier_1_cout, multiplier_1_out,
       multiplier_2_out, multiplier_3_out, multiplier_4_cout, out_add, out_and, out_divu, out_mulh,
       out_mulhu, out_mult, out_or, out_remu, out_sll, out_sra, out_srl, out_sub, out_xor;

  // Probe on 32'h7fffffff
  // Probe on {32{1'b1}}
  // Probe on {32{1'b1}}
  // Probe on 32'h7fffffff
  Multiplier #(.width(32)) multiplier_1 (
    .a({32{1'b1}}), .b(32'h7fffffff), .out(multiplier_1_out), .cout(multiplier_1_cout));  // open: cin
  // Probe on multiplier_1_cout
  // Probe on multiplier_1_out
  // Probe on multiplier_1_out
  // Probe on multiplier_1_out
  Adder #(.width(32)) adder_1 (.a(A), .b(B), .out(out_add));  // open: cin, cout
  assign out_and = A & B;  // AND_Gate and_1, 32 bits wide
  assign out_or = A | B;  // OR_Gate or_1, 32 bits wide
  assign out_xor = A ^ B;  // XOR_Gate xor_1, 32 bits wide
  Shifter #(.width(32), .shift("lr")) shifter_1 (.in(A), .\dist (B[4:0]), .out(out_srl));
  Shifter #(.width(32), .shift("ar")) shifter_2 (.in(A), .\dist (B[4:0]), .out(out_sra));
  Shifter #(.width(32)) shifter_3 (.in(A), .\dist (B[4:0]), .out(out_sll));
  assign bit_extender_1_out = {{31{A[31]}}, A[31]};  // Bit_Extender bit_extender_1
  assign bit_extender_2_out = {{31{B[31]}}, B[31]};  // Bit_Extender bit_extender_2
  Multiplier #(.width(32)) multiplier_2 (.a(bit_extender_1_out), .b(B), .out(multiplier_2_out));  // open: cin, cout
  Multiplier #(.width(32)) multiplier_3 (.a(A), .b(bit_extender_2_out), .out(multiplier_3_out));  // open: cin, cout
  Multiplier #(.width(32)) multiplier_4 (.a(A), .b(B), .cout(multiplier_4_cout));  // open: out, cin
  Adder #(.width(32)) adder_2 (.a(multiplier_2_out), .b(multiplier_3_out), .out(adder_2_out));  // open: cin, cout
  Adder #(.width(32)) adder_3 (.a(multiplier_4_cout), .b(adder_2_out), .out(out_mulh));  // open: cin, cout
  Comparator #(.width(32)) comparator_1 (.a(A), .b(B), .lt(out_slt[0]));  // open: gt, eq
  Divider #(.width(32)) divider_1 (.a(A), .b(B), .out(out_divu));  // open: upper, rem
  Divider #(.width(32)) divider_2 (.a(A), .b(B), .rem(out_remu));  // open: out, upper
  Multiplier #(.width(32)) multiplier_5 (.a(A), .b(B), .out(out_mult));  // open: cin, cout
  Multiplier #(.width(32)) multiplier_6 (.a(A), .b(B), .cout(out_mulhu));  // open: out, cin
  Subtractor #(.width(32)) subtractor_1 (.a(A), .b(B), .out(out_sub));  // open: bin, bout
  BitAdder #(.width(32)) bitadder_1 (.in0(A), .in1(B), .out(out_cnto));
  Multiplexer #(.select(4), .width(32), .enable("false")) multiplexer_1 (
    .in0(out_add), .in1(out_and), .in2(out_or), .in3(out_xor), .in4(out_srl), .in5(out_sra), .in6(out_sll),
    .in7({{31{1'b0}}, out_slt[0]}), .in8(out_divu), .in9(out_remu), .in10(out_mult), .in11(out_mulhu),
    .in12(out_sub), .in13({{25{1'b0}}, out_cnto}), .in14(out_mulh), .out(Result), .sel(ALUSel));  // open: in15

  // Other names for the same wires on the sheet: B5[4:0] = B[4:0]

  // Notes on the sheet:
  //   INPUTS to your circuit
  //   Preprocess input
  //   DON'T CHANGE THE LOCATIONS OF THE INPUTS AND OUTPUTS!
  //   Arithmetic Operators
  //   MULH
  //   OUTPUT from your circuit
  //   MUX Selector
endmodule
