// Logisim project control.circ as structural Verilog: 1 circuit, main circuit CONTROL
module CONTROL (
  input  [31:0] Inst,
  input  BrEq,
  input  BrLT,
  output PCSel,
  output InstSel,
  output [2:0] ImmSel,
  output RegWEn,
  output BrUn,
  output [1:0] ASel,
  output BSel,
  output [3:0] ALUSel,
  output MemRW,
  output [1:0] DataSel,
  output [1:0] WBSel
);

  wire AIType, AluAdd, AluAnd, AluDivu, AluMulh, AluMulhu, AluMult, AluOr, AluRemu, AluSll, AluSlt, AluSra,
       AluSrl, AluSub, AluXor, and_1_out, and_2_out, and_3_out, and_4_out, and_7_out, BType, comparator_9_eq,
       comparator_10_eq, comparator_11_eq, comparator_12_eq, comparator_13_eq, comparator_14_eq,
       comparator_15_gt, comparator_16_eq, comparator_17_eq, comparator_18_eq, comparator_19_eq,
       comparator_20_eq, comparator_21_eq, comparator_22_eq, comparator_23_eq, comparator_24_eq,
       comparator_25_eq, comparator_26_eq, comparator_27_eq, comparator_28_eq, comparator_29_eq,
       comparator_30_eq, comparator_31_eq, comparator_32_eq, comparator_33_eq, comparator_34_eq,
       comparator_35_eq, comparator_36_eq, comparator_37_eq, comparator_38_eq, comparator_39_eq,
       comparator_40_eq, comparator_41_eq, comparator_42_eq, comparator_43_eq, comparator_44_eq,
       comparator_45_eq, IType, JIType, JType, LIType, not_1_out, not_4_out, or_3_out, or_4_out, or_6_out,
       or_7_out, or_9_out, or_10_out, PCAluB, PCAluJ, RType, SType, UType;
  wire [1:0] multiplexer_2_out, multiplexer_8_out, multiplexer_9_out, multiplexer_10_out;
  wire [2:0] multiplexer_1_out, multiplexer_3_out, multiplexer_5_out, multiplexer_6_out;
  wire [3:0] multiplexer_14_out, multiplexer_15_out, multiplexer_16_out, multiplexer_17_out,
       multiplexer_18_out, multiplexer_19_out, multiplexer_20_out, multiplexer_21_out, multiplexer_22_out,
       multiplexer_23_out, multiplexer_24_out, multiplexer_25_out;
  wire [6:0] funct7_EX;

  Comparator #(.width(7)) comparator_1 (.a(Inst[6:0]), .b(7'b0110011), .eq(RType));  // open: gt, lt
  Comparator #(.width(7)) comparator_2 (.a(Inst[6:0]), .b(7'b0000011), .eq(LIType));  // open: gt, lt
  Comparator #(.width(7)) comparator_3 (.a(Inst[6:0]), .b(7'b0010011), .eq(AIType));  // open: gt, lt
  Comparator #(.width(7)) comparator_4 (.a(Inst[6:0]), .b(7'b0100011), .eq(SType));  // open: gt, lt
  Comparator #(.width(7)) comparator_5 (.a(Inst[6:0]), .b(7'b1100011), .eq(BType));  // open: gt, lt
  Comparator #(.width(7)) comparator_6 (.a(Inst[6:0]), .b(7'b0110111), .eq(UType));  // open: gt, lt
  Comparator #(.width(7)) comparator_7 (.a(Inst[6:0]), .b(7'b1101111), .eq(JType));  // open: gt, lt
  Comparator #(.width(7)) comparator_8 (.a(Inst[6:0]), .b(7'b1100111), .eq(JIType));  // open: gt, lt
  or or_1 (IType, LIType, AIType, JIType);
  Comparator #(.width(3)) comparator_9 (.a(Inst[14:12]), .b(3'b000), .eq(comparator_9_eq));  // open: gt, lt
  Comparator #(.width(3)) comparator_10 (.a(Inst[14:12]), .b(3'b100), .eq(comparator_10_eq));  // open: gt, lt
  Comparator #(.width(3)) comparator_11 (.a(Inst[14:12]), .b(3'b110), .eq(comparator_11_eq));  // open: gt, lt
  not not_1 (not_1_out, BrEq);
  Comparator #(.width(3)) comparator_12 (.a(Inst[14:12]), .b(3'b001), .eq(comparator_12_eq));  // open: gt, lt
  or or_2 (PCAluJ, JType, JIType);
  Multiplexer #(.width(3), .enable("false")) multiplexer_1 (
    .in0(3'b000), .in1(3'b000), .out(multiplexer_1_out), .sel(IType));
  and and_1 (and_1_out, BrEq, comparator_9_eq);
  and and_2 (and_2_out, BrLT, comparator_10_eq);
  and and_3 (and_3_out, BrLT, comparator_11_eq);
  and and_4 (and_4_out, not_1_out, comparator_12_eq);
  Multiplexer #(.width(2), .enable("false")) multiplexer_2 (
    .in0(2'b01), .in1(2'b00), .out(multiplexer_2_out), .sel(LIType));
  or or_3 (or_3_out, JIType, JType);
  Multiplexer #(.width(3), .enable("false")) multiplexer_3 (
    .in0(multiplexer_1_out), .in1(3'b001), .out(multiplexer_3_out), .sel(SType));
  Multiplexer #(.width(2), .enable("false")) multiplexer_4 (
    .in0(multiplexer_2_out), .in1(2'b10), .out(WBSel), .sel(or_3_out));
  or or_4 (or_4_out, and_1_out, and_2_out, and_3_out, and_4_out);
  Multiplexer #(.width(3), .enable("false")) multiplexer_5 (
    .in0(multiplexer_3_out), .in1(3'b010), .out(multiplexer_5_out), .sel(BType));
  or or_5 (InstSel, PCAluJ, PCAluB);
  Multiplexer #(.width(3), .enable("false")) multiplexer_6 (
    .in0(multiplexer_5_out), .in1(3'b011), .out(multiplexer_6_out), .sel(UType));
  and and_5 (PCAluB, BType, or_4_out);
  Multiplexer #(.width(3), .enable("false")) multiplexer_7 (
    .in0(multiplexer_6_out), .in1(3'b100), .out(ImmSel), .sel(JType));
  or or_6 (or_6_out, BType, JType);
  Multiplexer #(.width(2), .enable("false")) multiplexer_8 (
    .in0(2'b00), .in1(2'b00), .out(multiplexer_8_out), .sel(comparator_13_eq));
  Comparator #(.width(3)) comparator_13 (.a(Inst[14:12]), .b(3'b000), .eq(comparator_13_eq));  // open: gt, lt
  Comparator #(.width(3)) comparator_14 (.a(Inst[14:12]), .b(3'b001), .eq(comparator_14_eq));  // open: gt, lt
  or or_7 (or_7_out, BType, SType);
  Comparator #(.width(3)) comparator_15 (.a(Inst[14:12]), .b(3'b110), .gt(comparator_15_gt));  // open: eq, lt
  Multiplexer #(.width(2), .enable("false")) multiplexer_9 (
    .in0(2'b00), .in1(2'b01), .out(multiplexer_9_out), .sel(or_6_out));
  not not_2 (BSel, RType);
  or or_8 (MemRW, LIType, SType);
  Multiplexer #(.width(2), .enable("false")) multiplexer_10 (
    .in0(multiplexer_8_out), .in1(2'b10), .out(multiplexer_10_out), .sel(comparator_14_eq));
  Multiplexer #(.width(2), .enable("false")) multiplexer_11 (
    .in0(multiplexer_10_out), .in1(2'b11), .out(DataSel), .sel(comparator_16_eq));
  Comparator #(.width(3)) comparator_16 (.a(Inst[14:12]), .b(3'b010), .eq(comparator_16_eq));  // open: gt, lt
  not not_3 (RegWEn, or_7_out);
  and and_6 (BrUn, BType, comparator_15_gt);
  Multiplexer #(.width(2), .enable("false")) multiplexer_12 (
    .in0(multiplexer_9_out), .in1(2'b10), .out(ASel), .sel(UType));
  Comparator #(.width(3)) comparator_17 (.a(Inst[14:12]), .b(3'b101), .eq(comparator_17_eq));  // open: gt, lt
  or or_9 (or_9_out, AIType, RType);
  Comparator #(.width(7)) comparator_18 (.a(funct7_EX), .b({7{1'b0}}), .eq(comparator_18_eq));  // open: gt, lt
  Comparator #(.width(3)) comparator_19 (.a(Inst[14:12]), .b(3'b000), .eq(comparator_19_eq));  // open: gt, lt
  Comparator #(.width(7)) comparator_20 (.a(funct7_EX), .b({7{1'b0}}), .eq(comparator_20_eq));  // open: gt, lt
  Comparator #(.width(3)) comparator_21 (.a(Inst[14:12]), .b(3'b111), .eq(comparator_21_eq));  // open: gt, lt
  Comparator #(.width(7)) comparator_22 (.a(funct7_EX), .b({7{1'b0}}), .eq(comparator_22_eq));  // open: gt, lt
  Comparator #(.width(3)) comparator_23 (.a(Inst[14:12]), .b(3'b110), .eq(comparator_23_eq));  // open: gt, lt
  Comparator #(.width(7)) comparator_24 (.a(funct7_EX), .b({7{1'b0}}), .eq(comparator_24_eq));  // open: gt, lt
  Comparator #(.width(3)) comparator_25 (.a(Inst[14:12]), .b(3'b100), .eq(comparator_25_eq));  // open: gt, lt
  Comparator #(.width(7)) comparator_26 (.a(funct7_EX), .b({7{1'b0}}), .eq(comparator_26_eq));  // open: gt, lt
  Comparator #(.width(3)) comparator_27 (.a(Inst[14:12]), .b(3'b101), .eq(comparator_27_eq));  // open: gt, lt
  Comparator #(.width(7)) comparator_28 (.a(funct7_EX), .b(7'b0100000), .eq(comparator_28_eq));  // open: gt, lt
  Comparator #(.width(3)) comparator_29 (.a(Inst[14:12]), .b(3'b101), .eq(comparator_29_eq));  // open: gt, lt
  Comparator #(.width(7)) comparator_30 (.a(funct7_EX), .b({7{1'b0}}), .eq(comparator_30_eq));  // open: gt, lt
  Comparator #(.width(3)) comparator_31 (.a(Inst[14:12]), .b(3'b001), .eq(comparator_31_eq));  // open: gt, lt
  Comparator #(.width(7)) comparator_32 (.a(funct7_EX), .b({7{1'b0}}), .eq(comparator_32_eq));  // open: gt, lt
  Comparator #(.width(3)) comparator_33 (.a(Inst[14:12]), .b(3'b010), .eq(comparator_33_eq));  // open: gt, lt
  Comparator #(.width(7)) comparator_34 (.a(funct7_EX), .b(7'b0000001), .eq(comparator_34_eq));  // open: gt, lt
  Comparator #(.width(3)) comparator_35 (.a(Inst[14:12]), .b(3'b101), .eq(comparator_35_eq));  // open: gt, lt
  Comparator #(.width(7)) comparator_36 (.a(funct7_EX), .b(7'b0000001), .eq(comparator_36_eq));  // open: gt, lt
  Comparator #(.width(3)) comparator_37 (.a(Inst[14:12]), .b(3'b111), .eq(comparator_37_eq));  // open: gt, lt
  Comparator #(.width(7)) comparator_38 (.a(funct7_EX), .b(7'b0000001), .eq(comparator_38_eq));  // open: gt, lt
  Comparator #(.width(3)) comparator_39 (.a(Inst[14:12]), .b(3'b000), .eq(comparator_39_eq));  // open: gt, lt
  Comparator #(.width(7)) comparator_40 (.a(funct7_EX), .b(7'b0000001), .eq(comparator_40_eq));  // open: gt, lt
  Comparator #(.width(3)) comparator_41 (.a(Inst[14:12]), .b(3'b011), .eq(comparator_41_eq));  // open: gt, lt
  Comparator #(.width(7)) comparator_42 (.a(funct7_EX), .b(7'b0100000), .eq(comparator_42_eq));  // open: gt, lt
  Comparator #(.width(3)) comparator_43 (.a(Inst[14:12]), .b(3'b000), .eq(comparator_43_eq));  // open: gt, lt
  Comparator #(.width(7)) comparator_44 (.a(funct7_EX), .b(7'b0000001), .eq(comparator_44_eq));  // open: gt, lt
  Comparator #(.width(3)) comparator_45 (.a(Inst[14:12]), .b(3'b001), .eq(comparator_45_eq));  // open: gt, lt
  Multiplexer #(.width(7), .enable("false")) multiplexer_13 (
    .in0({7{1'b0}}), .in1(Inst[31:25]), .out(funct7_EX), .sel(or_10_out));
  or or_10 (or_10_out, comparator_17_eq, RType);
  not not_4 (not_4_out, or_9_out);
  and and_7 (and_7_out, comparator_18_eq, comparator_19_eq);
  and and_8 (AluAnd, comparator_20_eq, comparator_21_eq);
  and and_9 (AluOr, comparator_22_eq, comparator_23_eq);
  and and_10 (AluXor, comparator_24_eq, comparator_25_eq);
  and and_11 (AluSrl, comparator_26_eq, comparator_27_eq);
  and and_12 (AluSra, comparator_28_eq, comparator_29_eq);
  and and_13 (AluSll, comparator_30_eq, comparator_31_eq);
  and and_14 (AluSlt, comparator_32_eq, comparator_33_eq);
  and and_15 (AluDivu, comparator_34_eq, comparator_35_eq);
  and and_16 (AluRemu, comparator_36_eq, comparator_37_eq);
  and and_17 (AluMult, comparator_38_eq, comparator_39_eq);
  and and_18 (AluMulhu, comparator_40_eq, comparator_41_eq);
  and and_19 (AluSub, comparator_42_eq, comparator_43_eq);
  and and_20 (AluMulh, comparator_44_eq, comparator_45_eq);
  or or_11 (AluAdd, not_4_out, and_7_out);
  Multiplexer #(.width(4), .enable("false")) multiplexer_14 (
    .in0(4'b0000), .in1(4'b0001), .out(multiplexer_14_out), .sel(AluAnd));
  Multiplexer #(.width(4), .enable("false")) multiplexer_15 (
    .in0(multiplexer_14_out), .in1(4'b0010), .out(multiplexer_15_out), .sel(AluOr));
  Multiplexer #(.width(4), .enable("false")) multiplexer_16 (
    .in0(multiplexer_15_out), .in1(4'b0011), .out(multiplexer_16_out), .sel(AluXor));
  Multiplexer #(.width(4), .enable("false")) multiplexer_17 (
    .in0(multiplexer_16_out), .in1(4'b0100), .out(multiplexer_17_out), .sel(AluSrl));
  Multiplexer #(.width(4), .enable("false")) multiplexer_18 (
    .in0(multiplexer_17_out), .in1(4'b0101), .out(multiplexer_18_out), .sel(AluSra));
  Multiplexer #(.width(4), .enable("false")) multiplexer_19 (
    .in0(multiplexer_18_out), .in1(4'b0110), .out(multiplexer_19_out), .sel(AluSll));
  Multiplexer #(.width(4), .enable("false")) multiplexer_20 (
    .in0(multiplexer_19_out), .in1(4'b0111), .out(multiplexer_20_out), .sel(AluSlt));
  Multiplexer #(.width(4), .enable("false")) multiplexer_21 (
    .in0(multiplexer_20_out), .in1(4'b1000), .out(multiplexer_21_out), .sel(AluDivu));
  Multiplexer #(.width(4), .enable("false")) multiplexer_22 (
    .in0(multiplexer_21_out), .in1(4'b1001), .out(multiplexer_22_out), .sel(AluRemu));
  Multiplexer #(.width(4), .enable("false")) multiplexer_23 (
    .in0(multiplexer_22_out), .in1(4'b1010), .out(multiplexer_23_out), .sel(AluMult));
  Multiplexer #(.width(4), .enable("false")) multiplexer_24 (
    .in0(multiplexer_23_out), .in1(4'b1011), .out(multiplexer_24_out), .sel(AluMulhu));
  Multiplexer #(.width(4), .enable("false")) multiplexer_25 (
    .in0(multiplexer_24_out), .in1(4'b1100), .out(multiplexer_25_out), .sel(AluSub));
  Multiplexer #(.width(4), .enable("false")) multiplexer_26 (
    .in0(multiplexer_25_out), .in1(4'b1110), .out(ALUSel), .sel(AluSub));

  assign PCSel = InstSel;

  // Other names for the same wires on the sheet: Opcode[6:0] = Inst[6:0]; funct3[2:0] = Inst[14:12];
  //   funct7[6:0] = Inst[31:25]

  // Notes on the sheet:
  //   Load I-Type
  //   Arithmetic I-Type
  //   Jump I-Type
  //   jal
  //   jalr
  //   beq
  //   blt
  //   bltu
  //   bne
  //   Mem: 0, alu: 1, pc+4:2
  //   I-type: 0; S-type: 1; B-type: 2; U-type: 3; J-type: 4
  //   WBSel
  //   ImmSel
  //   PCSel
  //   lb: 0, lh: 1, lw:2
  //   RegWEn
  //   Reg: 0, PC: 1, Zero:2
  //   Reg: 0, Imm: 1
  //   BrUn
  //   ASel
  //   BSel
  //   MemRW
  //   DataSel
  //   ALUSel
endmodule
