// Logisim project regfile.circ as structural Verilog: 2 circuits, main circuit main
module main (
  input  [4:0] rs1,
  input  [4:0] rs2,
  input  [4:0] rd,
  input  [31:0] Write_Data,
  input  RegWEn,
  input  clk,
  output [31:0] ra,
  output [31:0] sp,
  output [31:0] t0,
  output [31:0] t1,
  output [31:0] t2,
  output [31:0] s0,
  output [31:0] s1,
  output [31:0] a0,
  output [31:0] Read_Data_1,
  output [31:0] Read_Data_2
);

  wire demultiplexer_1_out1, demultiplexer_1_out2, demultiplexer_1_out5, demultiplexer_1_out6,
       demultiplexer_1_out7, demultiplexer_1_out8, demultiplexer_1_out9, demultiplexer_1_out10;
  wire [31:0] x1_in, x2_in, x5_in, x6_in, x7_in, x8_in, x9_in, x10_in, zero;

  Multiplexer #(.select(5), .width(32), .enable("false")) multiplexer_1 (
    .in0(zero), .in1(ra), .in2(sp), .in5(t0), .in6(t1), .in7(t2), .in8(s0), .in9(s1), .in10(a0),
    .out(Read_Data_1), .sel(rs1));  // open: in3, in4, in11, in12, in13, in14, in15, in16, in17, in18, in19, in20, in21, in22, in23, in24, in25, in26, in27, in28, in29, in30, in31
  Multiplexer #(.select(5), .width(32), .enable("false")) multiplexer_2 (
    .in0(zero), .in1(ra), .in2(sp), .in5(t0), .in6(t1), .in7(t2), .in8(s0), .in9(s1), .in10(a0),
    .out(Read_Data_2), .sel(rs2));  // open: in3, in4, in11, in12, in13, in14, in15, in16, in17, in18, in19, in20, in21, in22, in23, in24, in25, in26, in27, in28, in29, in30, in31
  Demultiplexer #(.select(5), .enable("false")) demultiplexer_1 (
    .out1(demultiplexer_1_out1), .out2(demultiplexer_1_out2), .out5(demultiplexer_1_out5),
    .out6(demultiplexer_1_out6), .out7(demultiplexer_1_out7), .out8(demultiplexer_1_out8),
    .out9(demultiplexer_1_out9), .out10(demultiplexer_1_out10), .in(1'b1), .sel(rd));  // open: out0, out3, out4, out11, out12, out13, out14, out15, out16, out17, out18, out19, out20, out21, out22, out23, out24, out25, out26, out27, out28, out29, out30, out31
  Multiplexer #(.width(32), .enable("false")) multiplexer_3 (
    .in0(ra), .in1(Write_Data), .out(x1_in), .sel(demultiplexer_1_out1));
  Multiplexer #(.width(32), .enable("false")) multiplexer_4 (
    .in0(sp), .in1(Write_Data), .out(x2_in), .sel(demultiplexer_1_out2));
  Multiplexer #(.width(32), .enable("false")) multiplexer_5 (
    .in0(t0), .in1(Write_Data), .out(x5_in), .sel(demultiplexer_1_out5));
  Multiplexer #(.width(32), .enable("false")) multiplexer_6 (
    .in0(t1), .in1(Write_Data), .out(x6_in), .sel(demultiplexer_1_out6));
  registers registers_1 (
    .WrEn(RegWEn), .CLK(clk), .x1_in(x1_in), .x2_in(x2_in), .x3_in(x5_in), .x4_in(x6_in), .x5_in(x7_in),
    .x6_in(x8_in), .x7_in(x9_in), .x8_in(x10_in), .x0_out(zero), .x1_out(ra), .x2_out(sp), .x3_out(t0),
    .x4_out(t1), .x5_out(t2), .x6_out(s0), .x7_out(s1), .x8_out(a0));
  Multiplexer #(.width(32), .enable("false")) multiplexer_7 (
    .in0(t2), .in1(Write_Data), .out(x7_in), .sel(demultiplexer_1_out7));
  Multiplexer #(.width(32), .enable("false")) multiplexer_8 (
    .in0(s0), .in1(Write_Data), .out(x8_in), .sel(demultiplexer_1_out8));
  Multiplexer #(.width(32), .enable("false")) multiplexer_9 (
    .in0(s1), .in1(Write_Data), .out(x9_in), .sel(demultiplexer_1_out9));
  Multiplexer #(.width(32), .enable("false")) multiplexer_10 (
    .in0(a0), .in1(Write_Data), .out(x10_in), .sel(demultiplexer_1_out10));

  // Other names for the same wires on the sheet: read_data1[31:0] = Read_Data_1; read_data2[31:0] = Read_Data_2;
  //   read_reg1[4:0] = rs1; read_reg2[4:0] = rs2; write_en = RegWEn; write_reg[4:0] = rd

  // Notes on the sheet:
  //   INPUTS to your circuit
  //   Read data
  //   DON'T CHANGE THE LOCATIONS OF THE INPUTS AND OUTPUTS!
  //   These are DEBUG/TEST outputs from your circuit.
  //   Write data
  //   OUTPUTS from your circuit
endmodule

module registers (
  input  WrEn,
  input  CLK,
  input  [31:0] x1_in,
  input  [31:0] x2_in,
  input  [31:0] x3_in,
  input  [31:0] x4_in,
  input  [31:0] x5_in,
  input  [31:0] x6_in,
  input  [31:0] x7_in,
  input  [31:0] x8_in,
  output [31:0] x0_out,
  output [31:0] x1_out,
  output [31:0] x2_out,
  output [31:0] x3_out,
  output [31:0] x4_out,
  output [31:0] x5_out,
  output [31:0] x6_out,
  output [31:0] x7_out,
  output [31:0] x8_out
);

  Register #(.width(32)) register_1 (.D({32{1'b0}}), .en(1'b0), .clk(CLK), .Q(x0_out));  // open: clr
  Register #(.width(32)) register_2 (.D(x1_in), .en(WrEn), .clk(CLK), .Q(x1_out));  // open: clr
  Register #(.width(32)) register_3 (.D(x2_in), .en(WrEn), .clk(CLK), .Q(x2_out));  // open: clr
  Register #(.width(32)) register_4 (.D(x3_in), .en(WrEn), .clk(CLK), .Q(x3_out));  // open: clr
  Register #(.width(32)) register_5 (.D(x4_in), .en(WrEn), .clk(CLK), .Q(x4_out));  // open: clr
  Register #(.width(32)) register_6 (.D(x5_in), .en(WrEn), .clk(CLK), .Q(x5_out));  // open: clr
  Register #(.width(32)) register_7 (.D(x6_in), .en(WrEn), .clk(CLK), .Q(x6_out));  // open: clr
  Register #(.width(32)) register_8 (.D(x7_in), .en(WrEn), .clk(CLK), .Q(x7_out));  // open: clr
  Register #(.width(32)) register_9 (.D(x8_in), .en(WrEn), .clk(CLK), .Q(x8_out));  // open: clr

  // Notes on the sheet:
  //   x0_const
endmodule
