// Logisim project cpu.circ as structural Verilog: 4 circuits, main circuit main
module main (
  input  [31:0] INSTRUCTION,
  input  CLOCK,
  output [31:0] FETCH_ADDRESS,
  output [31:0] ra,
  output [31:0] sp,
  output [31:0] t0,
  output [31:0] t1,
  output [31:0] t2,
  output [31:0] s0,
  output [31:0] s1,
  output [31:0] a0
);

  wire BrEq, BrLT, BrUn, BSel, InstSel, MemRW, PCSel, RegWEn;
  wire [1:0] ASel, DataSel, WBSel;
  wire [2:0] ImmSel;
  wire [3:0] ALUSel;
  wire [31:0] adder_1_out, demultiplexer_1_out0, demultiplexer_1_out1, DMEM_p5, Inst, m_alu, m_DataA,
       m_DataB, m_Imm, m_mem, m_pc, m_pc_plus_4, m_wb, multiplexer_1_out, multiplexer_2_out,
       multiplexer_4_out, multiplexer_5_out, PC_F_q;

  Adder #(.width(32)) adder_1 (.a(PC_F_q), .b(32'h4), .out(adder_1_out));  // open: cin, cout
  Multiplexer #(.width(32), .enable("false")) multiplexer_1 (
    .in0(adder_1_out), .in1(m_alu), .out(multiplexer_1_out), .sel(PCSel));
  Multiplexer #(.width(32), .enable("false")) multiplexer_2 (
    .in0(INSTRUCTION), .in1(32'h13), .out(multiplexer_2_out), .sel(InstSel));
  Register #(.width(32)) PC_F (.D(multiplexer_1_out), .clk(CLOCK), .Q(PC_F_q));  // open: en, clr
  Register #(.width(32)) Inst_D (.D(multiplexer_2_out), .clk(CLOCK), .Q(Inst));  // open: en, clr
  CONTROL control_1 (
    .out_11(ALUSel), .out_10(BSel), .out_9(ASel), .out_8(BrUn), .out_7(RegWEn), .out_6(ImmSel),
    .out_5(PCSel), .out_4(InstSel), .in_3(BrLT), .in_2(BrEq), .in_1(Inst), .out_12(MemRW), .out_13(DataSel),
    .out_14(WBSel));
  Register #(.width(32)) PC_D (.D(PC_F_q), .clk(CLOCK), .Q(m_pc));  // open: en, clr
  Shifter #(.width(32), .shift("lr")) shifter_1 (.in(PC_F_q), .\dist (5'b00010), .out(FETCH_ADDRESS));
  // Probe on ImmSel
  // Probe on ASel
  // Probe on BSel
  // Probe on MemRW
  // Probe on WBSel
  Adder #(.width(32)) adder_2 (.a(m_pc), .b(32'h4), .out(m_pc_plus_4));  // open: cin, cout
  // Probe on BrUn
  // Probe on PCSel
  // Probe on ALUSel
  // Probe on DataSel
  // Probe on Inst
  Multiplexer #(.select(2), .width(32), .enable("false")) multiplexer_3 (
    .in0(m_mem), .in1(m_alu), .in2(m_pc_plus_4), .out(m_wb), .sel(WBSel));  // open: in3
  BRANCH_COMP branch_comp_1 (.Data_A(m_DataA), .Data_B(m_DataB), .BrUn(BrUn), .BrEq(BrEq), .BrLT(BrLT));
  // mem_main DMEM: pin names not known; wires that end beside it: m_alu, m_DataB, MemRW, CLOCK, DMEM_p5
  Demultiplexer #(.select(2), .width(32), .enable("false")) demultiplexer_1 (
    .out0(demultiplexer_1_out0), .out1(demultiplexer_1_out1), .out2(m_mem), .in(DMEM_p5), .sel(DataSel));  // open: out3
  IMM_GEN imm_gen_1 (.IMM_INPUT(Inst[31:7]), .IMM_SEL(ImmSel), .IMM_OUTPUT(m_Imm));
  // Probe on m_Imm
  assign m_mem = {{24{demultiplexer_1_out0[7]}}, demultiplexer_1_out0[7:0]};  // Bit_Extender bit_extender_1
  assign m_mem = {{16{demultiplexer_1_out1[15]}}, demultiplexer_1_out1[15:0]};  // Bit_Extender bit_extender_2
  Multiplexer #(.select(2), .width(32), .enable("false")) multiplexer_4 (
    .in0(m_DataA), .in1(m_pc), .in2({32{1'b0}}), .out(multiplexer_4_out), .sel(ASel));  // open: in3
  Multiplexer #(.width(32), .enable("false")) multiplexer_5 (
    .in0(m_DataB), .in1(m_Imm), .out(multiplexer_5_out), .sel(BSel));
  alu Arithmetic_Logic_Unit (.A(multiplexer_4_out), .B(multiplexer_5_out), .ALUSel(ALUSel), .Result(m_alu));
  regfile_main RegFile (
    .rs2(Inst[24:20]), .rd(Inst[11:7]), .Read_Data_1(m_DataA), .Read_Data_2(m_DataB), .ra(ra), .sp(sp),
    .t0(t0), .t1(t1), .t2(t2), .s0(s0), .s1(s1), .a0(a0), .rs1(Inst[19:15]), .Write_Data(m_wb),
    .RegWEn(RegWEn), .clk(CLOCK));

  // Other names for the same wires on the sheet: clk = CLOCK; fetch_addr[31:0] = FETCH_ADDRESS;
  //   m_AddrD[4:0] = Inst[11:7]; m_AddrA[4:0] = Inst[19:15]; m_AddrB[4:0] = Inst[24:20]

  // Notes on the sheet:
  //   Output
  //   Inputs/Outputs from run.circ. DO NOT MOVE THESE.
  //   Instruction Fetch
  //   Inputs
  //   Memory Access
  //   Register Write
  //   Inputs/Outputs from run.circ. DO NOT MOVE THESE.
  //   Execute
  //   Instruction Decode
endmodule

module IMM_GEN (
  input  [24:0] IMM_INPUT,
  input  [2:0] IMM_SEL,
  output [31:0] IMM_OUTPUT
);

  wire [31:0] bit_extender_1_out, bit_extender_2_out, bit_extender_3_out, bit_extender_4_out;

  assign bit_extender_1_out = {{20{IMM_INPUT[24]}}, IMM_INPUT[24:13]};  // Bit_Extender bit_extender_1
  assign bit_extender_2_out = {{20{IMM_INPUT[24]}}, {IMM_INPUT[24:18], IMM_INPUT[4:0]}};  // Bit_Extender bit_extender_2
  assign bit_extender_3_out = {{18{IMM_INPUT[24]}}, {IMM_INPUT[24], IMM_INPUT[0], IMM_INPUT[23:18], IMM_INPUT[4:1], 2'b00}};  // Bit_Extender bit_extender_3
  assign bit_extender_4_out = {{10{IMM_INPUT[24]}}, {IMM_INPUT[24], IMM_INPUT[12:5], IMM_INPUT[13], IMM_INPUT[23:14], 2'b00}};  // Bit_Extender bit_extender_4
  Multiplexer #(.select(3), .width(32), .enable("false")) multiplexer_1 (
    .in0(bit_extender_1_out), .in1(bit_extender_2_out), .in2(bit_extender_3_out),
    .in3({IMM_INPUT[24:5], {12{1'b0}}}), .in4(bit_extender_4_out), .out(IMM_OUTPUT), .sel(IMM_SEL));  // open: in5, in6, in7

  // Notes on the sheet:
  //   I
  //   S
  //   B
  //   U
  //   J
endmodule

module BRANCH_COMP (
  input  [31:0] Data_A,
  input  [31:0] Data_B,
  input  BrUn,
  output BrEq,
  output BrLT
);

  wire comparator_1_eq, comparator_1_lt, comparator_2_eq, comparator_2_lt;

  Comparator #(.width(32)) comparator_1 (
    .a(Data_A), .b(Data_B), .eq(comparator_1_eq), .lt(comparator_1_lt));  // open: gt
  Comparator #(.width(32), .mode("unsigned")) comparator_2 (
    .a(Data_A), .b(Data_B), .eq(comparator_2_eq), .lt(comparator_2_lt));  // open: gt
  Multiplexer #(.enable("false")) multiplexer_1 (.in0(comparator_1_eq), .in1(comparator_2_eq), .out(BrEq), .sel(BrUn));
  Multiplexer #(.enable("false")) multiplexer_2 (.in0(comparator_1_lt), .in1(comparator_2_lt), .out(BrLT), .sel(BrUn));
endmodule

module CONTROL (
  input  [31:0] in_1,
  input  in_2,
  input  in_3,
  output out_4,
  output out_5,
  output [2:0] out_6,
  output out_7,
  output out_8,
  output [1:0] out_9,
  output out_10,
  output [3:0] out_11,
  output out_12,
  output [1:0] out_13,
  output [1:0] out_14
);

  wire AIType, AluAdd, AluAnd, AluDivu, AluMulh, AluMulhu, AluMult, AluOr, AluRemu, AluSll, AluSlt, AluSra,
       AluSrl, AluSub, AluXor, and_1_out, and_2_out, and_3_out, and_4_out, and_20_out, BType,
       comparator_9_eq, comparator_10_eq, comparator_11_eq, comparator_12_eq, comparator_13_eq,
       comparator_14_eq, comparator_15_gt, comparator_16_eq, comparator_17_eq, comparator_18_eq,
       comparator_19_eq, comparator_20_eq, comparator_21_eq, comparator_22_eq, comparator_23_eq,
       comparator_24_eq, comparator_25_eq, comparator_26_eq, comparator_27_eq, comparator_28_eq,
       comparator_29_eq, comparator_30_eq, comparator_31_eq, comparator_32_eq, comparator_33_eq,
       comparator_34_eq, comparator_35_eq, comparator_36_eq, comparator_37_eq, comparator_38_eq,
       comparator_39_eq, comparator_40_eq, comparator_41_eq, comparator_42_eq, comparator_43_eq,
       comparator_44_eq, comparator_45_eq, IType, JIType, JType, LIType, not_1_out, not_4_out, or_3_out,
       or_4_out, or_6_out, or_7_out, or_9_out, or_10_out, PCAluB, PCAluJ, RType, SType, UType;
  wire [1:0] multiplexer_2_out, multiplexer_8_out, multiplexer_9_out, multiplexer_10_out;
  wire [2:0] multiplexer_1_out, multiplexer_3_out, multiplexer_5_out, multiplexer_6_out;
  wire [3:0] multiplexer_14_out, multiplexer_15_out, multiplexer_16_out, multiplexer_17_out,
       multiplexer_18_out, multiplexer_19_out, multiplexer_20_out, multiplexer_21_out, multiplexer_22_out,
       multiplexer_23_out, multiplexer_24_out, multiplexer_25_out, multiplexer_26_out;
  wire [6:0] funct7_EX;

  Comparator #(.width(7)) comparator_1 (.a(in_1[6:0]), .b(7'b0110011), .eq(RType));  // open: gt, lt
  Comparator #(.width(7)) comparator_2 (.a(in_1[6:0]), .b(7'b0000011), .eq(LIType));  // open: gt, lt
  Comparator #(.width(7)) comparator_3 (.a(in_1[6:0]), .b(7'b0010011), .eq(AIType));  // open: gt, lt
  Comparator #(.width(7)) comparator_4 (.a(in_1[6:0]), .b(7'b0100011), .eq(SType));  // open: gt, lt
  Comparator #(.width(7)) comparator_5 (.a(in_1[6:0]), .b(7'b1100011), .eq(BType));  // open: gt, lt
  Comparator #(.width(7)) comparator_6 (.a(in_1[6:0]), .b(7'b0110111), .eq(UType));  // open: gt, lt
  Comparator #(.width(7)) comparator_7 (.a(in_1[6:0]), .b(7'b1101111), .eq(JType));  // open: gt, lt
  Comparator #(.width(7)) comparator_8 (.a(in_1[6:0]), .b(7'b1100111), .eq(JIType));  // open: gt, lt
  or or_1 (IType, LIType, AIType, JIType);
  Comparator #(.width(3)) comparator_9 (.a(in_1[14:12]), .b(3'b000), .eq(comparator_9_eq));  // open: gt, lt
  Comparator #(.width(3)) comparator_10 (.a(in_1[14:12]), .b(3'b100), .eq(comparator_10_eq));  // open: gt, lt
  Comparator #(.width(3)) comparator_11 (.a(in_1[14:12]), .b(3'b110), .eq(comparator_11_eq));  // open: gt, lt
  not not_1 (not_1_out, in_2);
  Comparator #(.width(3)) comparator_12 (.a(in_1[14:12]), .b(3'b001), .eq(comparator_12_eq));  // open: gt, lt
  or or_2 (PCAluJ, JType, JIType);
  Multiplexer #(.width(3), .enable("false")) multiplexer_1 (
    .in0(3'b000), .in1(3'b000), .out(multiplexer_1_out), .sel(IType));
  and and_1 (and_1_out, in_2, comparator_9_eq);
  and and_2 (and_2_out, in_3, comparator_10_eq);
  and and_3 (and_3_out, in_3, comparator_11_eq);
  and and_4 (and_4_out, not_1_out, comparator_12_eq);
  Multiplexer #(.width(2), .enable("false")) multiplexer_2 (
    .in0(2'b01), .in1(2'b00), .out(multiplexer_2_out), .sel(LIType));
  or or_3 (or_3_out, JIType, JType);
  Multiplexer #(.width(3), .enable("false")) multiplexer_3 (
    .in0(multiplexer_1_out), .in1(3'b001), .out(multiplexer_3_out), .sel(SType));
  Multiplexer #(.width(2), .enable("false")) multiplexer_4 (
    .in0(multiplexer_2_out), .in1(2'b10), .out(out_14), .sel(or_3_out));
  or or_4 (or_4_out, and_1_out, and_2_out, and_3_out, and_4_out);
  Multiplexer #(.width(3), .enable("false")) multiplexer_5 (
    .in0(multiplexer_3_out), .in1(3'b010), .out(multiplexer_5_out), .sel(BType));
  or or_5 (out_4, PCAluJ, PCAluB);
  Multiplexer #(.width(3), .enable("false")) multiplexer_6 (
    .in0(multiplexer_5_out), .in1(3'b011), .out(multiplexer_6_out), .sel(UType));
  and and_5 (PCAluB, BType, or_4_out);
  Multiplexer #(.width(3), .enable("false")) multiplexer_7 (
    .in0(multiplexer_6_out), .in1(3'b100), .out(out_6), .sel(JType));
  or or_6 (or_6_out, BType, JType);
  Multiplexer #(.width(2), .enable("false")) multiplexer_8 (
    .in0(2'b00), .in1(2'b00), .out(multiplexer_8_out), .sel(comparator_13_eq));
  Comparator #(.width(3)) comparator_13 (.a(in_1[14:12]), .b(3'b000), .eq(comparator_13_eq));  // open: gt, lt
  Comparator #(.width(3)) comparator_14 (.a(in_1[14:12]), .b(3'b001), .eq(comparator_14_eq));  // open: gt, lt
  or or_7 (or_7_out, BType, SType);
  Comparator #(.width(3)) comparator_15 (.a(in_1[14:12]), .b(3'b110), .gt(comparator_15_gt));  // open: eq, lt
  Multiplexer #(.width(2), .enable("false")) multiplexer_9 (
    .in0(2'b00), .in1(2'b01), .out(multiplexer_9_out), .sel(or_6_out));
  not not_2 (out_10, RType);
  or or_8 (out_12, LIType, SType);
  Multiplexer #(.width(2), .enable("false")) multiplexer_10 (
    .in0(multiplexer_8_out), .in1(2'b10), .out(multiplexer_10_out), .sel(comparator_14_eq));
  Multiplexer #(.width(2), .enable("false")) multiplexer_11 (
    .in0(multiplexer_10_out), .in1(2'b11), .out(out_13), .sel(comparator_16_eq));
  Comparator #(.width(3)) comparator_16 (.a(in_1[14:12]), .b(3'b010), .eq(comparator_16_eq));  // open: gt, lt
  not not_3 (out_7, or_7_out);
  and and_6 (out_8, BType, comparator_15_gt);
  Multiplexer #(.width(2), .enable("false")) multiplexer_12 (
    .in0(multiplexer_9_out), .in1(2'b10), .out(out_9), .sel(UType));
  Comparator #(.width(3)) comparator_17 (.a(in_1[14:12]), .b(3'b101), .eq(comparator_17_eq));  // open: gt, lt
  Comparator #(.width(7)) comparator_18 (.a(funct7_EX), .b({7{1'b0}}), .eq(comparator_18_eq));  // open: gt, lt
  Comparator #(.width(3)) comparator_19 (.a(in_1[14:12]), .b(3'b111), .eq(comparator_19_eq));  // open: gt, lt
  Comparator #(.width(7)) comparator_20 (.a(funct7_EX), .b({7{1'b0}}), .eq(comparator_20_eq));  // open: gt, lt
  Comparator #(.width(3)) comparator_21 (.a(in_1[14:12]), .b(3'b110), .eq(comparator_21_eq));  // open: gt, lt
  Comparator #(.width(7)) comparator_22 (.a(funct7_EX), .b({7{1'b0}}), .eq(comparator_22_eq));  // open: gt, lt
  Comparator #(.width(3)) comparator_23 (.a(in_1[14:12]), .b(3'b100), .eq(comparator_23_eq));  // open: gt, lt
  Comparator #(.width(7)) comparator_24 (.a(funct7_EX), .b({7{1'b0}}), .eq(comparator_24_eq));  // open: gt, lt
  Comparator #(.width(3)) comparator_25 (.a(in_1[14:12]), .b(3'b101), .eq(comparator_25_eq));  // open: gt, lt
  Comparator #(.width(7)) comparator_26 (.a(funct7_EX), .b(7'b0100000), .eq(comparator_26_eq));  // open: gt, lt
  Comparator #(.width(3)) comparator_27 (.a(in_1[14:12]), .b(3'b101), .eq(comparator_27_eq));  // open: gt, lt
  Comparator #(.width(7)) comparator_28 (.a(funct7_EX), .b({7{1'b0}}), .eq(comparator_28_eq));  // open: gt, lt
  Comparator #(.width(3)) comparator_29 (.a(in_1[14:12]), .b(3'b001), .eq(comparator_29_eq));  // open: gt, lt
  Comparator #(.width(7)) comparator_30 (.a(funct7_EX), .b({7{1'b0}}), .eq(comparator_30_eq));  // open: gt, lt
  Comparator #(.width(3)) comparator_31 (.a(in_1[14:12]), .b(3'b010), .eq(comparator_31_eq));  // open: gt, lt
  Comparator #(.width(7)) comparator_32 (.a(funct7_EX), .b(7'b0000001), .eq(comparator_32_eq));  // open: gt, lt
  Comparator #(.width(3)) comparator_33 (.a(in_1[14:12]), .b(3'b101), .eq(comparator_33_eq));  // open: gt, lt
  Comparator #(.width(7)) comparator_34 (.a(funct7_EX), .b(7'b0000001), .eq(comparator_34_eq));  // open: gt, lt
  Comparator #(.width(3)) comparator_35 (.a(in_1[14:12]), .b(3'b111), .eq(comparator_35_eq));  // open: gt, lt
  Comparator #(.width(7)) comparator_36 (.a(funct7_EX), .b(7'b0000001), .eq(comparator_36_eq));  // open: gt, lt
  Comparator #(.width(3)) comparator_37 (.a(in_1[14:12]), .b(3'b000), .eq(comparator_37_eq));  // open: gt, lt
  Comparator #(.width(7)) comparator_38 (.a(funct7_EX), .b(7'b0000001), .eq(comparator_38_eq));  // open: gt, lt
  Comparator #(.width(3)) comparator_39 (.a(in_1[14:12]), .b(3'b011), .eq(comparator_39_eq));  // open: gt, lt
  Comparator #(.width(7)) comparator_40 (.a(funct7_EX), .b(7'b0100000), .eq(comparator_40_eq));  // open: gt, lt
  Comparator #(.width(3)) comparator_41 (.a(in_1[14:12]), .b(3'b000), .eq(comparator_41_eq));  // open: gt, lt
  Comparator #(.width(7)) comparator_42 (.a(funct7_EX), .b(7'b0000001), .eq(comparator_42_eq));  // open: gt, lt
  Comparator #(.width(3)) comparator_43 (.a(in_1[14:12]), .b(3'b001), .eq(comparator_43_eq));  // open: gt, lt
  or or_9 (or_9_out, AIType, RType);
  Comparator #(.width(7)) comparator_44 (.a(funct7_EX), .b({7{1'b0}}), .eq(comparator_44_eq));  // open: gt, lt
  Comparator #(.width(3)) comparator_45 (.a(in_1[14:12]), .b(3'b000), .eq(comparator_45_eq));  // open: gt, lt
  Multiplexer #(.width(7), .enable("false")) multiplexer_13 (
    .in0({7{1'b0}}), .in1(in_1[31:25]), .out(funct7_EX), .sel(or_10_out));
  or or_10 (or_10_out, comparator_17_eq, RType);
  and and_7 (AluAnd, comparator_18_eq, comparator_19_eq);
  and and_8 (AluOr, comparator_20_eq, comparator_21_eq);
  and and_9 (AluXor, comparator_22_eq, comparator_23_eq);
  and and_10 (AluSrl, comparator_24_eq, comparator_25_eq);
  and and_11 (AluSra, comparator_26_eq, comparator_27_eq);
  and and_12 (AluSll, comparator_28_eq, comparator_29_eq);
  and and_13 (AluSlt, comparator_30_eq, comparator_31_eq);
  and and_14 (AluDivu, comparator_32_eq, comparator_33_eq);
  and and_15 (AluRemu, comparator_34_eq, comparator_35_eq);
  and and_16 (AluMult, comparator_36_eq, comparator_37_eq);
  and and_17 (AluMulhu, comparator_38_eq, comparator_39_eq);
  and and_18 (AluSub, comparator_40_eq, comparator_41_eq);
  and and_19 (AluMulh, comparator_42_eq, comparator_43_eq);
  not not_4 (not_4_out, or_9_out);
  and and_20 (and_20_out, comparator_44_eq, comparator_45_eq);
  or or_11 (AluAdd, not_4_out, and_20_out);
  Multiplexer #(.width(4), .enable("false")) multiplexer_14 (
    .in0(4'b0000), .in1(4'b0001), .out(multiplexer_14_out), .sel(AluAnd));
  Multiplexer #(.width(4), .enable("false")) multiplexer_15 (
    .in0(multiplexer_14_out), .in1(4'b0010), .out(multiplexer_15_out), .sel(AluOr));
  Multiplexer #(.width(4), .enable("false")) multiplexer_16 (
    .in0(multiplexer_15_out), .in1(4'b0011), .out(multiplexer_16_out), .sel(AluXor));
  Multiplexer #(.width(4), .enable("false")) multiplexer_17 (
    .in0(multiplexer_16_out), .in1(4'b0100), .out(multiplexer_17_out), .sel(AluSrl));
  Multiplexer #(.width(4), .enable("false")) multiplexer_18 (
    .in0(multiplexer_17_out), .in1(4'b0101), .out(multiplexer_18_out), .sel(AluSra));
  Multiplexer #(.width(4), .enable("false")) multiplexer_19 (
    .in0(multiplexer_18_out), .in1(4'b0110), .out(multiplexer_19_out), .sel(AluSll));
  Multiplexer #(.width(4), .enable("false")) multiplexer_20 (
    .in0(multiplexer_19_out), .in1(4'b0111), .out(multiplexer_20_out), .sel(AluSlt));
  Multiplexer #(.width(4), .enable("false")) multiplexer_21 (
    .in0(multiplexer_20_out), .in1(4'b1000), .out(multiplexer_21_out), .sel(AluDivu));
  Multiplexer #(.width(4), .enable("false")) multiplexer_22 (
    .in0(multiplexer_21_out), .in1(4'b1001), .out(multiplexer_22_out), .sel(AluRemu));
  Multiplexer #(.width(4), .enable("false")) multiplexer_23 (
    .in0(multiplexer_22_out), .in1(4'b1010), .out(multiplexer_23_out), .sel(AluMult));
  Multiplexer #(.width(4), .enable("false")) multiplexer_24 (
    .in0(multiplexer_23_out), .in1(4'b1011), .out(multiplexer_24_out), .sel(AluMulhu));
  Multiplexer #(.width(4), .enable("false")) multiplexer_25 (
    .in0(multiplexer_24_out), .in1(4'b1100), .out(multiplexer_25_out), .sel(AluSub));
  Multiplexer #(.width(4), .enable("false")) multiplexer_26 (
    .in0(multiplexer_25_out), .in1(4'b1110), .out(multiplexer_26_out), .sel(AluMulh));
  Multiplexer #(.width(4), .enable("false")) multiplexer_27 (
    .in0(multiplexer_26_out), .in1(4'b0000), .out(out_11), .sel(AluAdd));

  assign out_5 = out_4;

  // Other names for the same wires on the sheet: ALUSel[3:0] = out_11; ASel[1:0] = out_9; BrEq = in_2; BrLT = in_3;
  //   BrUn = out_8; BSel = out_10; DataSel[1:0] = out_13; ImmSel[2:0] = out_6; Inst[31:0] = in_1;
  //   Opcode[6:0] = in_1[6:0]; funct3[2:0] = in_1[14:12]; funct7[6:0] = in_1[31:25]; MemRW = out_12; InstSel = out_4;
  //   PCSel = out_4; RegWEn = out_7; WBSel[1:0] = out_14

  // Notes on the sheet:
  //   Load I-Type
  //   Arithmetic I-Type
  //   Jump I-Type
  //   jal
  //   jalr
  //   beq
  //   blt
  //   bltu
  //   bne
  //   Mem: 0, alu: 1, pc+4:2
  //   I-type: 0; S-type: 1; B-type: 2; U-type: 3; J-type: 4
  //   WBSel
  //   ImmSel
  //   PCSel
  //   lb: 0, lh: 1, lw:2
  //   RegWEn
  //   Reg: 0, PC: 1, Zero:2
  //   Reg: 0, Imm: 1
  //   BrUn
  //   ASel
  //   BSel
  //   MemRW
  //   DataSel
  //   ALUSel
endmodule
